# Fritzing sketch Candy-Dispenser (saved by Fritzing 0.9.3b)
breadboards: 1

parts:
  Part1 = Arduino Uno (Rev3)
  J1 = Basic Servo
  S1 = Round Pushbutton
  R1 = Resistor [tolerance=±5% resistance=220 package=THT]

nets:
  N1: Part1.D9_PWM, J1.pulse
  GND: Part1.GND, J1.gnd, R1.Pin_1
  N2: Part1.D2, S1.leg1, R1.Pin_0
  5V: Part1.5V, J1.vcc, S1.leg0
